# Fritzing sketch etoile-0v (saved by Fritzing 1.0.2)

parts:
  Point_0_V_commun_(carte_N2) = female pin header, 1 pin
  J31_BP_(SC944D) = female pin header, 4 pins
  J1_BA_SC942C = female pin header, 4 pins
  J2_BA_SC942C = female pin header, 4 pins
  J1_BA_SC941C = female pin header, 4 pins
  J2_BA_SC941C = female pin header, 4 pins
  J1_BA_SC940D = female pin header, 4 pins
  J2_BA_SC940D = female pin header, 4 pins

nets:
  0 V TBTS (non relié à la terre): Point_0_V_commun_(carte_N2).pin1, J31_BP_(SC944D).pin3, J1_BA_SC942C.pin3, J2_BA_SC942C.pin3, J1_BA_SC941C.pin3, J2_BA_SC941C.pin3, J1_BA_SC940D.pin3, J2_BA_SC940D.pin3

notes:
  Principe N2 : étoile 0 V doublée (proposition, non réalisée)
  Seule la broche 3 (0 V) de chaque connecteur est représentée. SDA, SCL et +15 V passent par la même carte de distribution, dans les mêmes faisceaux. Les câbles de chaînage actuels sont retirés.
  Chaque BA rejoint le point 0 V commun par deux faisceaux courts (J1 et J2, AWG20, 15 cm au plus) : les conducteurs sont doublés. Le BP y est relié par J31. On relie un 0 V à un autre 0 V, jamais au PE : la TBTS est conservée.
  Ordre de grandeur [déduit]
  Seuil d’équilibrage : ≈ 80 à 120 A en onde 8/20 et 50 à 65 A en front rapide, contre 20 et 11 A avec le chaînage actuel. Écart de masse statique entre cartes : moins de 0,02 V. À valider au banc.
  Sur la même carte, par port : PTC puis TVS du +15 V, et un cavalier pour retirer un BA mort du bus. Aucune retouche des BA ni du firmware.
  Étoile 0 V doublée (principe N2, proposition) : fils courts entre la broche 3 (0 V) de chaque connecteur et un point 0 V commun. SDA, SCL et +15 V (non représentés) passent par la même carte de distribution, dans les mêmes faisceaux. Les câbles de chaînage actuels sont retirés.
  Chaque BA arrive par J1 et J2 : deux fils 0 V en parallèle. Le BP arrive par J31. Liaison 0 V à 0 V uniquement, jamais vers la terre (PE).
  Seuil d’équilibrage estimé : ≈ 80 à 120 A (onde 8/20) et 50 à 65 A (front rapide), contre 20 et 11 A aujourd’hui [déduit, à valider au banc].
