# Fritzing sketch liaison-i2c-actuelle (saved by Fritzing 1.0.2)

parts:
  U19_PCA9306_(BP) = IC, DIP package, 8 pins [chip_label=PCA9306]
  U4_PIC16F946_(BA) = IC, DIP package, 10 pins [chip_label=PIC16F946]
  J31-1_SDA = female pin header, 1 pin
  J31-2_SCL = female pin header, 1 pin
  J31-3_0_V = female pin header, 1 pin
  J31-4_+15_V = female pin header, 1 pin
  J1-1_SDA = female pin header, 1 pin
  J1-2_SCL = female pin header, 1 pin
  J1-3_0_V = female pin header, 1 pin
  J1-4_+15_V = female pin header, 1 pin
  R156_1_kΩ = Resistor [resistance=1k package=THT]
  R155_1_kΩ = Resistor [resistance=1k package=THT]
  R2_0_Ω = Resistor [resistance=0 package=THT]
  R1_0_Ω = Resistor [resistance=0 package=THT]
  R41_10_kΩ = Resistor [resistance=10k package=THT]
  R40_10_kΩ = Resistor [resistance=10k package=THT]
  D33_TVS = Zener Diode [part_number=SMF5V0A package="300 mil [THT]"]
  D34_TVS = Zener Diode [part_number=SMF5V0A package="300 mil [THT]"]
  D2_TVS = Zener Diode [part_number=SMF5V0A package="300 mil [THT]"]
  D1_TVS = Zener Diode [part_number=SMF5V0A package="300 mil [THT]"]

nets:
  SCL1 : MCF52259: U19_PCA9306_(BP).pin3
  SDA1 : MCF52259: U19_PCA9306_(BP).pin4
  N1: U19_PCA9306_(BP).pin5, J31-1_SDA.pin1, J1-1_SDA.pin1, R155_1_kΩ.Pin_0, R1_0_Ω.Pin_0, D34_TVS.cathode, D1_TVS.cathode
  N2: U19_PCA9306_(BP).pin6, J31-2_SCL.pin1, J1-2_SCL.pin1, R156_1_kΩ.Pin_0, R2_0_Ω.Pin_0, D33_TVS.cathode, D2_TVS.cathode
  N3: U4_PIC16F946_(BA).pin1, R2_0_Ω.Pin_1, R41_10_kΩ.Pin_0
  N4: U4_PIC16F946_(BA).pin2, R1_0_Ω.Pin_1, R40_10_kΩ.Pin_0
  GND: U4_PIC16F946_(BA).pin5, J31-3_0_V.pin1, J1-3_0_V.pin1, D33_TVS.anode, D34_TVS.anode, D2_TVS.anode, D1_TVS.anode
  +5 V (BA): U4_PIC16F946_(BA).pin10, R41_10_kΩ.Pin_1, R40_10_kΩ.Pin_1
  +VBUS (+15 V)/BA_ALIM +15 V: J31-4_+15_V.pin1, J1-4_+15_V.pin1
  +5 VS (BP): R156_1_kΩ.Pin_1, R155_1_kΩ.Pin_1

notes:
  Liaison I2C BP ↔ BA : montage actuel
  Schéma simplifié d’après les schémas des cartes : BP = SC944D ; BA = SC940D (même topologie sur SC941C et SC942C, repères différents).
  Câble de bus, 4 conducteurs : 1 SDA, 2 SCL, 3 0 V, 4 +15 V. Les trois BA sont chaînés sur ce câble (J1 et J2 en parallèle).
  Non représentés : perles L30/L32 du BP, alimentations VREF/EN de U19, découplages, alimentation du BA (+VBUS vers son régulateur). U4 : numéros de broches du symbole générique ; broches réelles du PIC16F946 (TQFP-64) : RC6/SCL = 61, RC7/SDA = 62.
  R1, R2 = 0 Ω : aucune limitation de courant vers le PIC.
  La diode interne du PIC conduit (≈ 5,5 V) avant la TVS (6,4 V) : c’est le PIC qui écrête, sans limite de courant (tenue : ±20 mA) [fiche technique].
  TVS SMF5V0A : seuil 6,4 à 7,1 V ; 9,2 V à 21,7 A en onde 10/1000 [fiche technique]. Le PCA9306 ne tient que 7 V : il partage le courant avec la TVS.
  Carte BP (SC944D) : U19 adapte les niveaux 3,3 V / 5 V ; R155/R156 tirent SDA/SCL au +5 VS ; D33/D34 (TVS SMF5V0A) écrêtent vers le 0 V près du connecteur J31.
  Carte BA (SC940D ; SC941C et SC942C identiques) : D1/D2 (TVS) près du connecteur J1, R1/R2 en série (0 Ω), R40/R41 tirent SDA/SCL au +5 V du BA, puis le PIC.
  Câble de bus (J31 ↔ J1) : bleu = SDA, jaune = SCL, noir = 0 V, orange = +15 V (BA_ALIM). Fils rouges : +5 V propre à chaque carte.
  R1, R2 = 0 Ω : aucune limitation de courant.
  La diode interne du PIC conduit (≈ 5,5 V) avant la TVS (6,4 V) : c’est le PIC qui encaisse le courant.
