# Fritzing sketch liaison-i2c-renforcee (saved by Fritzing 1.0.2)

parts:
  U19_PCA9306_(BP) = IC, DIP package, 8 pins [chip_label=PCA9306]
  U4_PIC16F946_(BA) = IC, DIP package, 10 pins [chip_label=PIC16F946]
  J31-1_SDA = female pin header, 1 pin
  J31-2_SCL = female pin header, 1 pin
  J31-3_0_V = female pin header, 1 pin
  J31-4_+15_V = female pin header, 1 pin
  J1-1_SDA = female pin header, 1 pin
  J1-2_SCL = female pin header, 1 pin
  J1-3_0_V = female pin header, 1 pin
  J1-4_+15_V = female pin header, 1 pin
  R156_1_kΩ = Resistor [resistance=1k package=THT]
  R155_1_kΩ = Resistor [resistance=1k package=THT]
  R2_47_Ω = Resistor [resistance=47 package=THT]
  R1_47_Ω = Resistor [resistance=47 package=THT]
  R41_10_kΩ = Resistor [resistance=10k package=THT]
  R40_10_kΩ = Resistor [resistance=10k package=THT]
  D33_TVS = Zener Diode [part_number=SMF5V0A package="300 mil [THT]"]
  D34_TVS = Zener Diode [part_number=SMF5V0A package="300 mil [THT]"]
  D2_TVS = Zener Diode [part_number=SMF5V0A package="300 mil [THT]"]
  D1_TVS = Zener Diode [part_number=SMF5V0A package="300 mil [THT]"]
  BAT54S_(SCL)_haut = Schottky Diode [part_number=BAT54S package="300 mil [THT]"]
  BAT54S_(SCL) = Schottky Diode [part_number=BAT54S package="300 mil [THT]"]
  BAT54S_(SDA)_haut = Schottky Diode [part_number=BAT54S package="300 mil [THT]"]
  BAT54S_(SDA) = Schottky Diode [part_number=BAT54S package="300 mil [THT]"]

nets:
  SCL1 : MCF52259: U19_PCA9306_(BP).pin3
  SDA1 : MCF52259: U19_PCA9306_(BP).pin4
  N1: U19_PCA9306_(BP).pin5, J31-1_SDA.pin1, J1-1_SDA.pin1, R155_1_kΩ.Pin_0, R1_47_Ω.Pin_0, D34_TVS.cathode, D1_TVS.cathode
  N2: U19_PCA9306_(BP).pin6, J31-2_SCL.pin1, J1-2_SCL.pin1, R156_1_kΩ.Pin_0, R2_47_Ω.Pin_0, D33_TVS.cathode, D2_TVS.cathode
  N3: U4_PIC16F946_(BA).pin1, R2_47_Ω.Pin_1, R41_10_kΩ.Pin_0, BAT54S_(SCL)_haut.anode, BAT54S_(SCL).cathode
  N4: U4_PIC16F946_(BA).pin2, R1_47_Ω.Pin_1, R40_10_kΩ.Pin_0, BAT54S_(SDA)_haut.anode, BAT54S_(SDA).cathode
  GND: U4_PIC16F946_(BA).pin5, J31-3_0_V.pin1, J1-3_0_V.pin1, D33_TVS.anode, D34_TVS.anode, D2_TVS.anode, D1_TVS.anode, BAT54S_(SCL).anode, BAT54S_(SDA).anode
  +5 V (BA): U4_PIC16F946_(BA).pin10, R41_10_kΩ.Pin_1, R40_10_kΩ.Pin_1, BAT54S_(SCL)_haut.cathode, BAT54S_(SDA)_haut.cathode
  +VBUS (+15 V)/BA_ALIM +15 V: J31-4_+15_V.pin1, J1-4_+15_V.pin1
  +5 VS (BP): R156_1_kΩ.Pin_1, R155_1_kΩ.Pin_1

notes:
  Liaison I2C BP ↔ BA : montage renforcé proposé (P1 + option P2 côté BA)
  Schéma simplifié d’après les schémas des cartes : BP = SC944D ; BA = SC940D (même topologie sur SC941C et SC942C, repères différents).
  Câble de bus, 4 conducteurs : 1 SDA, 2 SCL, 3 0 V, 4 +15 V. Les trois BA sont chaînés sur ce câble (J1 et J2 en parallèle).
  Non représentés : perles L30/L32 du BP, alimentations VREF/EN de U19, découplages, alimentation du BA (+VBUS vers son régulateur). U4 : numéros de broches du symbole générique ; broches réelles du PIC16F946 (TQFP-64) : RC6/SCL = 61, RC7/SDA = 62.
  R1, R2 = 47 Ω anti-impulsion (0805). Au-delà du seuil, la TVS absorbe l’essentiel : le courant dans le PIC est limité. Critère : écart de masse mesuré ≤ 0,1 V, sinon étoile 0 V (N2) d’abord, ou 33 Ω.
  BAT54S sur les empreintes C23/C25 (22 pF non montés), cathode au +5 V. À VC = 12 V : (12 − 5,7) / 47 ≈ 135 mA dans la Schottky au lieu du PIC [déduit, à valider au banc].
  Côté BP inchangé ici. L’option P2 complète ajoute au BP 2,2 kΩ, 47 Ω et une BAT54S, après relevé à l’oscilloscope. 47 Ω seul : 19 à 34 mA au seuil de la TVS [déduit].
  Carte BP (SC944D) : U19 adapte les niveaux 3,3 V / 5 V ; R155/R156 tirent SDA/SCL au +5 VS ; D33/D34 (TVS SMF5V0A) écrêtent vers le 0 V près du connecteur J31.
  Carte BA (SC940D ; SC941C et SC942C identiques) : D1/D2 (TVS) près du connecteur J1, R1/R2 en série (47 Ω), BAT54S, R40/R41 tirent SDA/SCL au +5 V du BA, puis le PIC.
  Câble de bus (J31 ↔ J1) : bleu = SDA, jaune = SCL, noir = 0 V, orange = +15 V (BA_ALIM). Fils rouges : +5 V propre à chaque carte.
  R1, R2 = 47 Ω anti-impulsion et BAT54S vers +5 V et 0 V, après la résistance. TVS D1/D2 conservées côté connecteur.
  La TVS absorbe l’essentiel ; le courant dans le PIC est limité (≈ 135 mA dérivés dans la Schottky à 12 V [déduit]).
